# Fritzing sketch esp32_propane_scale_v1 (saved by Fritzing 1.0.6)

parts:
  SparkFun_ESP32_Thing1 = SparkFun ESP32 Thing [part_number=DEV-13907]
  SparkFun_Load_Cell_Amplifier_-_HX1 = SparkFun Load Cell Amplifier - HX711 [part_number=SEN-13879]
  LR = Load Sensor - 50kg [part_number=SEN-10245]
  UL = Load Sensor - 50kg [part_number=SEN-10245]
  UR = Load Sensor - 50kg [part_number=SEN-10245]
  LL = Load Sensor - 50kg [part_number=SEN-10245]
  M1 = ESP-Prog [package=THT]  # not connected
  proto1 = adafruit
  LL_2 = screw terminal, 3 pins
  UR_2 = screw terminal, 3 pins
  LR_2 = screw terminal, 3 pins
  E+_E-_A-_A+ = screw terminal, 4 pins
  UL_2 = screw terminal, 3 pins
  A+_A-_E-_E+ = screw terminal, 4 pins
  G_C_D_5_3 = screw terminal, 5 pins

nets:
  GND: SparkFun_ESP32_Thing1.GND, SparkFun_Load_Cell_Amplifier_-_HX1.GND, E+_E-_A-_A+.pin3, A+_A-_E-_E+.pin2, G_C_D_5_3.pin1
  N1: SparkFun_ESP32_Thing1.VUSB-RAW, SparkFun_Load_Cell_Amplifier_-_HX1.VCC, G_C_D_5_3.pin4
  3.3V: SparkFun_ESP32_Thing1.3.3V, SparkFun_Load_Cell_Amplifier_-_HX1.VDD, G_C_D_5_3.pin5
  N2: SparkFun_ESP32_Thing1.16, SparkFun_Load_Cell_Amplifier_-_HX1.DAT, G_C_D_5_3.pin3
  N3: SparkFun_ESP32_Thing1.4, SparkFun_Load_Cell_Amplifier_-_HX1.SCK, G_C_D_5_3.pin2
  N4: SparkFun_Load_Cell_Amplifier_-_HX1.A+, E+_E-_A-_A+.pin1, A+_A-_E-_E+.pin4
  N5: SparkFun_Load_Cell_Amplifier_-_HX1.A-, E+_E-_A-_A+.pin2, A+_A-_E-_E+.pin3
  N6: SparkFun_Load_Cell_Amplifier_-_HX1.AVDD, E+_E-_A-_A+.pin4, A+_A-_E-_E+.pin1
  N7: LR.B, LL_2.pin3
  N8: LR.W, LL_2.pin2
  N9: LR.R, LL_2.pin1
  N10: UL.B, UL_2.pin3
  N11: UL.W, UL_2.pin2
  N12: UL.R, UL_2.pin1
  N13: UR.B, LR_2.pin3
  N14: UR.W, LR_2.pin2
  N15: UR.R, LR_2.pin1
  N16: LL.B, UR_2.pin3
  N17: LL.W, UR_2.pin2
  N18: LL.R, UR_2.pin1
  N19: proto1.connectorC1, proto1.connectorH2
  N20: proto1.connectorC5, proto1.connectorH3
  N21: proto1.connectorC9, proto1.connectorH4
  N22: proto1.connectorC13, proto1.connectorH1
  N23: proto1.connectorE2, proto1.connectorE6
  N24: proto1.connectorE3, proto1.connectorE11
  N25: proto1.connectorE7, proto1.connectorE15
  N26: proto1.connectorE10, proto1.connectorE14

notes:
  +/White
  -/Black
  C/Red
  A+
  A-
  E-
  E+

custom parts:
  SparkFun ESP32 Thing: The SparkFun ESP32 Thing is a comprehensive development platform for Espressif’s ESP32, their super-charged version of the popular ESP8266. Like the 8266, the ESP32 is a WiFi-compatible microcontroller, but to that it adds support for Bluetooth low-energy (i.e BLE, BT4.0, Bluetooth Smart), and nearly 30 I/O pins. The ESP32’s power and versatility will make it the foundation of IoT and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
  SparkFun Load Cell Amplifier - HX711: The SparkFun Load Cell Amplifier is a small breakout board for the HX711 IC that allows you to easily read load cells to measure weight. By connecting the amplifier to your microcontroller you will be able to read the changes in the resistance of the load cell, and with some calibration you’ll be able to get very accurate weight measurements. This can be handy for creating your own industrial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
  Load Sensor - 50kg: Half-wheatstone bridge Load Cell modified from the Fritzing Repo This load sensor, sometimes called a strain gauge, is the same one found in digital bathroom scales (you know, the ones you use in January for your New Year's resolutions, and then forget about a month later). This sensor can measure up to about 110 pounds.
  ESP-Prog: Espressif ESP-Prog board. ESP-Prog is one of Espressif’s development and debugging tools, with functions including automatic firmware downloading, serial communication, and JTAG online debugging. ESP-Prog's automatic firmware downloading and serial communication functions are supported on both the ESP8266 and ESP32 platforms, while the JTAG online debugging is supported only on the ESP32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
