# Fritzing sketch esp32_propane_scale (saved by Fritzing 1.0.6)
breadboards: 1

parts:
  SparkFun_ESP32_Thing1 = SparkFun ESP32 Thing [part_number=DEV-13907]  # not connected
  Part2 = SparkFun Load Sensor Combinator
  SparkFun_Load_Cell_Amplifier_-_HX1 = SparkFun Load Cell Amplifier - HX711 [part_number=SEN-13879]
  S1 = Load Sensor - 50kg [part_number=SEN-10245]
  S2 = Load Sensor - 50kg [part_number=SEN-10245]
  S3 = Load Sensor - 50kg [part_number=SEN-10245]
  S4 = Load Sensor - 50kg [part_number=SEN-10245]
  M1 = ESP-Prog [package=THT]  # not connected
  J3 = screw terminal, 3 pins
  J4 = screw terminal, 3 pins
  J9 = screw terminal, 3 pins
  proto1 = adafruit
  J2 = screw terminal, 3 pins

nets:
  N1: Part2.1, proto1.connectorB11, proto1.connectorE3
  N2: Part2.2#1, Part2.2#4, proto1.connectorE2, proto1.connectorE6
  N3: Part2.E-, Part2.5, SparkFun_Load_Cell_Amplifier_-_HX1.GND, proto1.connectorE1
  N4: Part2.N$1, proto1.connectorB15, proto1.connectorE7
  N5: Part2.A-, SparkFun_Load_Cell_Amplifier_-_HX1.A-, proto1.connectorE5
  N6: Part2.2#7, Part2.2#10, proto1.connectorB10, proto1.connectorB14
  N7: Part2.A+, SparkFun_Load_Cell_Amplifier_-_HX1.A+, proto1.connectorB9
  N8: Part2.E+, SparkFun_Load_Cell_Amplifier_-_HX1.AVDD, proto1.connectorB13
  N9: S1.B, J9.pin3
  N10: S1.W, J9.pin2
  N11: S1.R, J9.pin1
  N12: S2.B, J2.pin3
  N13: S2.W, J2.pin2
  N14: S2.R, J2.pin1
  N15: S3.B, J3.pin3
  N16: S3.W, J3.pin2
  N17: S3.R, J3.pin1
  N18: S4.B, J4.pin3
  N19: S4.W, J4.pin2
  N20: S4.R, J4.pin1

custom parts:
  SparkFun ESP32 Thing: The SparkFun ESP32 Thing is a comprehensive development platform for Espressif’s ESP32, their super-charged version of the popular ESP8266. Like the 8266, the ESP32 is a WiFi-compatible microcontroller, but to that it adds support for Bluetooth low-energy (i.e BLE, BT4.0, Bluetooth Smart), and nearly 30 I/O pins. The ESP32’s power and versatility will make it the foundation of IoT and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
  SparkFun Load Cell Amplifier - HX711: The SparkFun Load Cell Amplifier is a small breakout board for the HX711 IC that allows you to easily read load cells to measure weight. By connecting the amplifier to your microcontroller you will be able to read the changes in the resistance of the load cell, and with some calibration you’ll be able to get very accurate weight measurements. This can be handy for creating your own industrial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
  Load Sensor - 50kg: Half-wheatstone bridge Load Cell modified from the Fritzing Repo This load sensor, sometimes called a strain gauge, is the same one found in digital bathroom scales (you know, the ones you use in January for your New Year's resolutions, and then forget about a month later). This sensor can measure up to about 110 pounds.
  ESP-Prog: Espressif ESP-Prog board. ESP-Prog is one of Espressif’s development and debugging tools, with functions including automatic firmware downloading, serial communication, and JTAG online debugging. ESP-Prog's automatic firmware downloading and serial communication functions are supported on both the ESP8266 and ESP32 platforms, while the JTAG online debugging is supported only on the ESP32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
